# Fritzing sketch Robot_Toy_cra_for_L298N (saved by Fritzing 0.9.2b)
perfboards: 1

parts:
  M1 = DC Motor
  M2 = DC Motor
  J1 = Basic Servo
  J2 = shrouded pin header, 20 pins [form="♂ (shrouded male)"]
  元件1 = HC-SR04
  元件2 = Bluetooth HC-06
  U1 = atmega168 [package=dip]
  C1 = Capacitor [package=cap-pth-small-kit]
  R1 = Resistor [tolerance=±5% resistance=10k package=THT]
  VCC2 = Battery
  Y1 = CRYSTAL [package=crystal-smd-10.5x4.8-2pin]
  C2 = Capacitor [package=cap-pth-small-kit]
  J3 = female pin header, 6 pins [form="♀ (female)"]
  J4 = screw terminal, 3 pins
  J5 = Screw terminal - 2 pins [package=THT]
  J6 = Screw terminal - 2 pins [package=THT]
  元件3 = DC-DC Power Module (5v)
  J8 = shrouded pin header, 20 pins [form="♂ (shrouded male)"]
  J9 = Screw terminal - 2 pins [package=THT]
  J10 = female pin header, 3 pins [form="♀ (female)"]
  J11 = female pin header, 3 pins [form="♀ (female)"]
  J12 = male pin header, 6 pins [form="♂ (male)"]

nets:
  N1: M1.pin_1, J5.pin2
  N2: M1.pin_2, J5.pin1
  N3: M2.pin_1, J6.pin2
  N4: M2.pin_2, J6.pin1
  N5: J1.gnd, J2.pin15
  N6: J1.vcc, J2.pin16
  N7: J1.pulse, J2.pin17
  N8: J2.pin1, J3.pin6
  N9: J2.pin2, J3.pin5
  N10: J2.pin3, J3.pin4
  N11: J2.pin4, J3.pin3
  N12: J2.pin5, J3.pin2
  N13: J2.pin6, J3.pin1
  N14: J2.pin7, 元件1.Gnd
  N15: J2.pin8, 元件1.Vcc
  N16: J2.pin9, 元件1.Echo
  N17: J2.pin10, 元件1.Trig
  N18: J2.pin11, 元件2.RXD
  N19: J2.pin12, 元件2.TXD
  N20: J2.pin13, 元件2.VCC
  N21: J2.pin14, 元件2.GND
  N22: J2.pin18, VCC2.-
  N23: J2.pin19, VCC2.+
  N24: J2.pin20, J4.pin1, 元件3.Vin
  N25: U1.RESET, R1.Pin_1
  N26: U1.D2, J8.pin11
  N27: U1.D3_(PWM), J8.pin6
  N28: U1.D4, J8.pin12
  N29: U1.VCC, U1.AVCC, U1.AREF, R1.Pin_0, J8.pin8, J8.pin13, J8.pin16, J9.pin1
  N30: U1.GND, C1.1, C2.2, J8.pin7, J8.pin14, J8.pin15, J9.pin2, J11.pin2
  N31: U1.XLAT1, C1.2, Y1.1
  N32: U1.XLAT2, Y1.2, C2.1
  N33: U1.D5_(PWM), J8.pin5
  N34: U1.D6_(PWM), J8.pin4
  N35: U1.D8, J8.pin17
  N36: U1.D9_(PWM), J8.pin3
  N37: U1.D10_(PWM), J8.pin2
  N38: U1.D11_(PWM), J8.pin1
  N39: U1.D12, J8.pin10
  N40: U1.D13, J8.pin9
  N41: U1.A0, J12.pin6
  N42: U1.A1, J12.pin5
  N43: U1.A2, J12.pin4
  N44: U1.A3, J12.pin3
  N45: U1.A4, J12.pin2
  N46: U1.A5, J12.pin1
  N47: 元件3.GND, 元件3.GND*
  N48: J8.pin18, J11.pin1
  N49: J8.pin19, J10.pin2
  N50: J8.pin20, J10.pin1

notes:
  E1 N1 N2 N3 N4 E2
  Rx   Tx   Vcc  Gnd  Gnd  Vcc  Ser  Vin- Vin+ Vin+
  Tr   Ec   Vcc  Gnd  E1   N1   N2   N3   N4   E2
  超音波測距HC-SR04
  Tr : 18(D12)
  Ec : 19 (D13)
  Vcc
  Gnd
  L298N控制板
  E1 : 5(D3)
  N1 : 11(D5)
  N2 : 12(D6)
  N3 : 15(D9)
  N4 : 16(D10)
  E2 : 17(D11)
  藍芽HC-06
  Rx : 4(D2)
  Tx : 6(D4)
  Vcc
  Gnd
  伺服馬達SG90
  Gnd
  Vcc
  Ser : 14(D8)
  Vin- 18650
  Vin+ 18650
  Vin+ to L298N&LM259
  大燈 : 23(A0)
  倒車 : 24(A1)
  左方 : 25(A2)
  右方 : 26(A3)
  煞車 : 27(A4)

custom parts:
  HC-SR04: HC-SR04 ultrasonic distance sensor
  Battery: Your standard 2x 18650 battery pack (7,4 Volts)
  DC-DC Power Module (5v): DC-DC Power Module based con AMS1117-5.0 Input: DC 6~12V (input power must higher 1V than output power); Output: 5V (+/-0.05V error), 800mA
